// Logisim project CA_HWP1_403106681.circ as structural Verilog: 1 circuit, main circuit main
module main (
  input  [31:0] A,
  input  [31:0] B,
  input  [2:0] ALU_Ctrl,
  output [31:0] Result_Lo,
  output Z,
  output C,
  output [31:0] Result_Hi,
  output V,
  output N
);

  wire ADD_S, ADD_U, and_2_out, and_5_out, and_6_out, comparator_1_eq, Cout, MUL, NOP, NOP1, NOP2, NOP3,
       not_2_out, not_3_out, not_4_out, not_5_out, not_6_out, not_7_out, not_8_out, not_9_out, not_10_out,
       SUB_S, SUB_U, xnor_1_out, xnor_2_out, xor_1_out, xor_3_out, xor_4_out;
  wire [30:0] or_2_out;
  wire [31:0] and_1_out, and_3_out, B_t, HIGH, LOW, multiplexer_2_out, multiplexer_4_out, multiplexer_5_out,
       multiplexer_6_out, multiplexer_7_out, multiplexer_8_out, multiplexer_9_out, multiplexer_10_out,
       multiplexer_11_out, multiplexer_12_out, multiplexer_13_out, multiplexer_14_out, multiplexer_15_out,
       multiplexer_16_out, multiplexer_17_out, multiplexer_18_out, multiplexer_19_out, multiplexer_20_out,
       multiplexer_21_out, multiplexer_22_out, multiplexer_23_out, multiplexer_24_out, multiplexer_25_out,
       multiplexer_26_out, multiplexer_27_out, multiplexer_28_out, multiplexer_29_out, multiplexer_30_out,
       multiplexer_31_out, multiplexer_32_out, multiplexer_33_out, multiplexer_34_out, multiplexer_35_out,
       not_1_out, S, xor_2_out;
  wire [63:0] adder_1_out, adder_2_out, adder_3_out, adder_4_out, adder_5_out, adder_6_out, adder_7_out,
       adder_8_out, adder_9_out, adder_10_out, adder_11_out, adder_12_out, adder_13_out, adder_14_out,
       adder_15_out, adder_16_out, adder_17_out, adder_18_out, adder_19_out, adder_20_out, adder_21_out,
       adder_22_out, adder_23_out, adder_24_out, adder_25_out, adder_26_out, adder_27_out, adder_28_out,
       adder_29_out, adder_30_out, bit_extender_1_out, bit_extender_2_out, bit_extender_3_out,
       bit_extender_4_out, bit_extender_5_out, bit_extender_6_out, bit_extender_7_out, bit_extender_8_out,
       bit_extender_9_out, bit_extender_10_out, bit_extender_11_out, bit_extender_12_out,
       bit_extender_13_out, bit_extender_14_out, bit_extender_15_out, bit_extender_16_out,
       bit_extender_17_out, bit_extender_18_out, bit_extender_19_out, bit_extender_20_out,
       bit_extender_21_out, bit_extender_22_out, bit_extender_23_out, bit_extender_24_out,
       bit_extender_25_out, bit_extender_26_out, bit_extender_27_out, bit_extender_28_out,
       bit_extender_29_out, bit_extender_30_out, bit_extender_31_out, bit_extender_32_out, shifter_1_out,
       shifter_2_out, shifter_3_out, shifter_4_out, shifter_5_out, shifter_6_out, shifter_7_out,
       shifter_8_out, shifter_9_out, shifter_10_out, shifter_11_out, shifter_12_out, shifter_13_out,
       shifter_14_out, shifter_15_out, shifter_16_out, shifter_17_out, shifter_18_out, shifter_19_out,
       shifter_20_out, shifter_21_out, shifter_22_out, shifter_23_out, shifter_24_out, shifter_25_out,
       shifter_26_out, shifter_27_out, shifter_28_out, shifter_29_out, shifter_30_out, shifter_31_out,
       shifter_32_out;

  assign not_1_out = ~B;  // NOT_Gate not_1, 32 bits wide
  Decoder #(.enable("false"), .select(3)) decoder_1 (
    .out0(ADD_U), .out1(ADD_S), .out2(SUB_U), .out3(SUB_S), .out4(MUL), .out5(NOP1), .out6(NOP2),
    .out7(NOP3), .sel(ALU_Ctrl));
  or or_1 (NOP, NOP1, NOP2, NOP3);
  Multiplexer #(.width(32)) multiplexer_1 (.in0(B), .in1(not_1_out), .out(B_t), .sel(ALU_Ctrl[1]));
  assign and_1_out = B_t & A;  // AND_Gate and_1, 32 bits wide
  xnor xnor_1 (xnor_1_out, Cout, ALU_Ctrl[1]);
  xor xor_1 (xor_1_out, Cout, ALU_Ctrl[1]);
  assign xor_2_out = B_t ^ A;  // XOR_Gate xor_2, 32 bits wide
  assign {Cout, or_2_out} = and_1_out | and_3_out;  // OR_Gate or_2, 32 bits wide
  Comparator #(.width(32)) comparator_1 (.a(S), .b({32{1'b0}}), .eq(comparator_1_eq));  // open: gt, lt
  not not_2 (not_2_out, ALU_Ctrl[0]);
  and and_2 (and_2_out, xor_1_out, not_2_out, not_3_out);
  not not_3 (not_3_out, ALU_Ctrl[2]);
  xor xor_3 (xor_3_out, S[31], A[31]);
  xnor xnor_2 (xnor_2_out, A[31], B_t[31]);
  xor xor_4 (xor_4_out, V, S[31]);
  assign and_3_out = xor_2_out & {or_2_out, ALU_Ctrl[1]};  // AND_Gate and_3, 32 bits wide
  not not_4 (not_4_out, NOP);
  not not_5 (not_5_out, C);
  not not_6 (not_6_out, ALU_Ctrl[2]);
  not not_7 (not_7_out, ALU_Ctrl[2]);
  assign S = {or_2_out, ALU_Ctrl[1]} ^ xor_2_out;  // XOR_Gate xor_5, 32 bits wide
  and and_4 (Z, not_4_out, not_5_out, comparator_1_eq);
  not not_8 (not_8_out, NOP);
  not not_9 (not_9_out, NOP);
  and and_5 (and_5_out, xor_3_out, not_6_out, xnor_2_out);
  not not_10 (not_10_out, NOP);
  and and_6 (and_6_out, xor_4_out, ALU_Ctrl[0], not_7_out);
  and and_7 (C, not_8_out, and_2_out);
  and and_8 (V, not_9_out, and_5_out);
  and and_9 (N, not_10_out, and_6_out);
  Multiplexer #(.width(32)) multiplexer_2 (.in0(S), .in1(LOW), .out(multiplexer_2_out), .sel(ALU_Ctrl[2]));
  Multiplexer #(.width(32)) multiplexer_3 (.in0({32{1'b0}}), .in1(HIGH), .out(Result_Hi), .sel(MUL));
  Multiplexer #(.width(32)) multiplexer_4 (.in0({32{1'b0}}), .in1(A), .out(multiplexer_4_out), .sel(B_t[0]));
  Multiplexer #(.width(32)) multiplexer_5 (.in0({32{1'b0}}), .in1(A), .out(multiplexer_5_out), .sel(B_t[1]));
  Multiplexer #(.width(32)) multiplexer_6 (.in0({32{1'b0}}), .in1(A), .out(multiplexer_6_out), .sel(B_t[2]));
  Multiplexer #(.width(32)) multiplexer_7 (.in0({32{1'b0}}), .in1(A), .out(multiplexer_7_out), .sel(B_t[3]));
  Multiplexer #(.width(32)) multiplexer_8 (.in0({32{1'b0}}), .in1(A), .out(multiplexer_8_out), .sel(B_t[4]));
  Multiplexer #(.width(32)) multiplexer_9 (.in0({32{1'b0}}), .in1(A), .out(multiplexer_9_out), .sel(B_t[5]));
  Multiplexer #(.width(32)) multiplexer_10 (.in0({32{1'b0}}), .in1(A), .out(multiplexer_10_out), .sel(B_t[6]));
  Multiplexer #(.width(32)) multiplexer_11 (.in0({32{1'b0}}), .in1(A), .out(multiplexer_11_out), .sel(B_t[7]));
  Multiplexer #(.width(32)) multiplexer_12 (.in0({32{1'b0}}), .in1(A), .out(multiplexer_12_out), .sel(B_t[8]));
  Multiplexer #(.width(32)) multiplexer_13 (.in0({32{1'b0}}), .in1(A), .out(multiplexer_13_out), .sel(B_t[9]));
  Multiplexer #(.width(32)) multiplexer_14 (.in0({32{1'b0}}), .in1(A), .out(multiplexer_14_out), .sel(B_t[10]));
  Multiplexer #(.width(32)) multiplexer_15 (.in0({32{1'b0}}), .in1(A), .out(multiplexer_15_out), .sel(B_t[11]));
  Multiplexer #(.width(32)) multiplexer_16 (.in0({32{1'b0}}), .in1(A), .out(multiplexer_16_out), .sel(B_t[12]));
  Multiplexer #(.width(32)) multiplexer_17 (.in0({32{1'b0}}), .in1(A), .out(multiplexer_17_out), .sel(B_t[13]));
  Multiplexer #(.width(32)) multiplexer_18 (.in0({32{1'b0}}), .in1(A), .out(multiplexer_18_out), .sel(B_t[14]));
  Multiplexer #(.width(32)) multiplexer_19 (.in0({32{1'b0}}), .in1(A), .out(multiplexer_19_out), .sel(B_t[15]));
  Multiplexer #(.width(32)) multiplexer_20 (.in0({32{1'b0}}), .in1(A), .out(multiplexer_20_out), .sel(B_t[16]));
  Multiplexer #(.width(32)) multiplexer_21 (.in0({32{1'b0}}), .in1(A), .out(multiplexer_21_out), .sel(B_t[17]));
  Multiplexer #(.width(32)) multiplexer_22 (.in0({32{1'b0}}), .in1(A), .out(multiplexer_22_out), .sel(B_t[18]));
  Multiplexer #(.width(32)) multiplexer_23 (.in0({32{1'b0}}), .in1(A), .out(multiplexer_23_out), .sel(B_t[19]));
  Multiplexer #(.width(32)) multiplexer_24 (.in0({32{1'b0}}), .in1(A), .out(multiplexer_24_out), .sel(B_t[20]));
  Multiplexer #(.width(32)) multiplexer_25 (.in0({32{1'b0}}), .in1(A), .out(multiplexer_25_out), .sel(B_t[21]));
  Multiplexer #(.width(32)) multiplexer_26 (.in0({32{1'b0}}), .in1(A), .out(multiplexer_26_out), .sel(B_t[22]));
  Multiplexer #(.width(32)) multiplexer_27 (.in0({32{1'b0}}), .in1(A), .out(multiplexer_27_out), .sel(B_t[23]));
  Multiplexer #(.width(32)) multiplexer_28 (.in0({32{1'b0}}), .in1(A), .out(multiplexer_28_out), .sel(B_t[24]));
  Multiplexer #(.width(32)) multiplexer_29 (.in0({32{1'b0}}), .in1(A), .out(multiplexer_29_out), .sel(B_t[25]));
  Multiplexer #(.width(32)) multiplexer_30 (.in0({32{1'b0}}), .in1(A), .out(multiplexer_30_out), .sel(B_t[26]));
  Multiplexer #(.width(32)) multiplexer_31 (.in0({32{1'b0}}), .in1(A), .out(multiplexer_31_out), .sel(B_t[27]));
  Multiplexer #(.width(32)) multiplexer_32 (.in0({32{1'b0}}), .in1(A), .out(multiplexer_32_out), .sel(B_t[28]));
  Multiplexer #(.width(32)) multiplexer_33 (.in0({32{1'b0}}), .in1(A), .out(multiplexer_33_out), .sel(B_t[29]));
  Multiplexer #(.width(32)) multiplexer_34 (.in0({32{1'b0}}), .in1(A), .out(multiplexer_34_out), .sel(B_t[30]));
  Multiplexer #(.width(32)) multiplexer_35 (.in0({32{1'b0}}), .in1(A), .out(multiplexer_35_out), .sel(B_t[31]));
  Multiplexer #(.width(32)) multiplexer_36 (.in0(multiplexer_2_out), .in1({32{1'b0}}), .out(Result_Lo), .sel(NOP));
  assign bit_extender_1_out = {{32{1'b0}}, multiplexer_4_out};  // Bit_Extender bit_extender_1
  assign bit_extender_2_out = {{32{1'b0}}, multiplexer_5_out};  // Bit_Extender bit_extender_2
  assign bit_extender_3_out = {{32{1'b0}}, multiplexer_6_out};  // Bit_Extender bit_extender_3
  assign bit_extender_4_out = {{32{1'b0}}, multiplexer_7_out};  // Bit_Extender bit_extender_4
  assign bit_extender_5_out = {{32{1'b0}}, multiplexer_8_out};  // Bit_Extender bit_extender_5
  assign bit_extender_6_out = {{32{1'b0}}, multiplexer_9_out};  // Bit_Extender bit_extender_6
  assign bit_extender_7_out = {{32{1'b0}}, multiplexer_10_out};  // Bit_Extender bit_extender_7
  assign bit_extender_8_out = {{32{1'b0}}, multiplexer_11_out};  // Bit_Extender bit_extender_8
  assign bit_extender_9_out = {{32{1'b0}}, multiplexer_12_out};  // Bit_Extender bit_extender_9
  assign bit_extender_10_out = {{32{1'b0}}, multiplexer_13_out};  // Bit_Extender bit_extender_10
  assign bit_extender_11_out = {{32{1'b0}}, multiplexer_14_out};  // Bit_Extender bit_extender_11
  assign bit_extender_12_out = {{32{1'b0}}, multiplexer_15_out};  // Bit_Extender bit_extender_12
  assign bit_extender_13_out = {{32{1'b0}}, multiplexer_16_out};  // Bit_Extender bit_extender_13
  assign bit_extender_14_out = {{32{1'b0}}, multiplexer_17_out};  // Bit_Extender bit_extender_14
  assign bit_extender_15_out = {{32{1'b0}}, multiplexer_18_out};  // Bit_Extender bit_extender_15
  assign bit_extender_16_out = {{32{1'b0}}, multiplexer_19_out};  // Bit_Extender bit_extender_16
  assign bit_extender_17_out = {{32{1'b0}}, multiplexer_20_out};  // Bit_Extender bit_extender_17
  assign bit_extender_18_out = {{32{1'b0}}, multiplexer_21_out};  // Bit_Extender bit_extender_18
  assign bit_extender_19_out = {{32{1'b0}}, multiplexer_22_out};  // Bit_Extender bit_extender_19
  assign bit_extender_20_out = {{32{1'b0}}, multiplexer_23_out};  // Bit_Extender bit_extender_20
  assign bit_extender_21_out = {{32{1'b0}}, multiplexer_24_out};  // Bit_Extender bit_extender_21
  assign bit_extender_22_out = {{32{1'b0}}, multiplexer_25_out};  // Bit_Extender bit_extender_22
  assign bit_extender_23_out = {{32{1'b0}}, multiplexer_26_out};  // Bit_Extender bit_extender_23
  assign bit_extender_24_out = {{32{1'b0}}, multiplexer_27_out};  // Bit_Extender bit_extender_24
  assign bit_extender_25_out = {{32{1'b0}}, multiplexer_28_out};  // Bit_Extender bit_extender_25
  assign bit_extender_26_out = {{32{1'b0}}, multiplexer_29_out};  // Bit_Extender bit_extender_26
  assign bit_extender_27_out = {{32{1'b0}}, multiplexer_30_out};  // Bit_Extender bit_extender_27
  assign bit_extender_28_out = {{32{1'b0}}, multiplexer_31_out};  // Bit_Extender bit_extender_28
  assign bit_extender_29_out = {{32{1'b0}}, multiplexer_32_out};  // Bit_Extender bit_extender_29
  assign bit_extender_30_out = {{32{1'b0}}, multiplexer_33_out};  // Bit_Extender bit_extender_30
  assign bit_extender_31_out = {{32{1'b0}}, multiplexer_34_out};  // Bit_Extender bit_extender_31
  assign bit_extender_32_out = {{32{1'b0}}, multiplexer_35_out};  // Bit_Extender bit_extender_32
  Shifter #(.width(64)) shifter_1 (.in(bit_extender_1_out), .\dist ({6{1'b0}}), .out(shifter_1_out));
  Shifter #(.width(64)) shifter_2 (.in(bit_extender_2_out), .\dist (6'b000001), .out(shifter_2_out));
  Shifter #(.width(64)) shifter_3 (.in(bit_extender_3_out), .\dist (6'b000010), .out(shifter_3_out));
  Shifter #(.width(64)) shifter_4 (.in(bit_extender_4_out), .\dist (6'b000011), .out(shifter_4_out));
  Shifter #(.width(64)) shifter_5 (.in(bit_extender_5_out), .\dist (6'b000100), .out(shifter_5_out));
  Shifter #(.width(64)) shifter_6 (.in(bit_extender_6_out), .\dist (6'b000101), .out(shifter_6_out));
  Shifter #(.width(64)) shifter_7 (.in(bit_extender_7_out), .\dist (6'b000110), .out(shifter_7_out));
  Shifter #(.width(64)) shifter_8 (.in(bit_extender_8_out), .\dist (6'b000111), .out(shifter_8_out));
  Shifter #(.width(64)) shifter_9 (.in(bit_extender_9_out), .\dist (6'b001000), .out(shifter_9_out));
  Shifter #(.width(64)) shifter_10 (.in(bit_extender_10_out), .\dist (6'b001001), .out(shifter_10_out));
  Shifter #(.width(64)) shifter_11 (.in(bit_extender_11_out), .\dist (6'b001010), .out(shifter_11_out));
  Shifter #(.width(64)) shifter_12 (.in(bit_extender_12_out), .\dist (6'b001011), .out(shifter_12_out));
  Shifter #(.width(64)) shifter_13 (.in(bit_extender_13_out), .\dist (6'b001100), .out(shifter_13_out));
  Shifter #(.width(64)) shifter_14 (.in(bit_extender_14_out), .\dist (6'b001101), .out(shifter_14_out));
  Shifter #(.width(64)) shifter_15 (.in(bit_extender_15_out), .\dist (6'b001110), .out(shifter_15_out));
  Shifter #(.width(64)) shifter_16 (.in(bit_extender_16_out), .\dist (6'b001111), .out(shifter_16_out));
  Shifter #(.width(64)) shifter_17 (.in(bit_extender_17_out), .\dist (6'b010000), .out(shifter_17_out));
  Shifter #(.width(64)) shifter_18 (.in(bit_extender_18_out), .\dist (6'b010001), .out(shifter_18_out));
  Shifter #(.width(64)) shifter_19 (.in(bit_extender_19_out), .\dist (6'b010010), .out(shifter_19_out));
  Shifter #(.width(64)) shifter_20 (.in(bit_extender_20_out), .\dist (6'b010011), .out(shifter_20_out));
  Shifter #(.width(64)) shifter_21 (.in(bit_extender_21_out), .\dist (6'b010100), .out(shifter_21_out));
  Shifter #(.width(64)) shifter_22 (.in(bit_extender_22_out), .\dist (6'b010101), .out(shifter_22_out));
  Shifter #(.width(64)) shifter_23 (.in(bit_extender_23_out), .\dist (6'b010110), .out(shifter_23_out));
  Shifter #(.width(64)) shifter_24 (.in(bit_extender_24_out), .\dist (6'b010111), .out(shifter_24_out));
  Shifter #(.width(64)) shifter_25 (.in(bit_extender_25_out), .\dist (6'b011000), .out(shifter_25_out));
  Shifter #(.width(64)) shifter_26 (.in(bit_extender_26_out), .\dist (6'b011001), .out(shifter_26_out));
  Shifter #(.width(64)) shifter_27 (.in(bit_extender_27_out), .\dist (6'b011010), .out(shifter_27_out));
  Shifter #(.width(64)) shifter_28 (.in(bit_extender_28_out), .\dist (6'b011011), .out(shifter_28_out));
  Shifter #(.width(64)) shifter_29 (.in(bit_extender_29_out), .\dist (6'b011100), .out(shifter_29_out));
  Shifter #(.width(64)) shifter_30 (.in(bit_extender_30_out), .\dist (6'b011101), .out(shifter_30_out));
  Shifter #(.width(64)) shifter_31 (.in(bit_extender_31_out), .\dist (6'b011110), .out(shifter_31_out));
  Shifter #(.width(64)) shifter_32 (.in(bit_extender_32_out), .\dist (6'b011111), .out(shifter_32_out));
  Adder #(.width(64)) adder_1 (.a(shifter_1_out), .b(shifter_2_out), .out(adder_1_out), .cin(1'b0));  // open: cout
  Adder #(.width(64)) adder_2 (.a(shifter_3_out), .b(shifter_4_out), .out(adder_2_out), .cin(1'b0));  // open: cout
  Adder #(.width(64)) adder_3 (.a(shifter_5_out), .b(shifter_6_out), .out(adder_3_out), .cin(1'b0));  // open: cout
  Adder #(.width(64)) adder_4 (.a(shifter_7_out), .b(shifter_8_out), .out(adder_4_out), .cin(1'b0));  // open: cout
  Adder #(.width(64)) adder_5 (.a(shifter_9_out), .b(shifter_10_out), .out(adder_5_out), .cin(1'b0));  // open: cout
  Adder #(.width(64)) adder_6 (.a(shifter_11_out), .b(shifter_12_out), .out(adder_6_out), .cin(1'b0));  // open: cout
  Adder #(.width(64)) adder_7 (.a(shifter_13_out), .b(shifter_14_out), .out(adder_7_out), .cin(1'b0));  // open: cout
  Adder #(.width(64)) adder_8 (.a(shifter_15_out), .b(shifter_16_out), .out(adder_8_out), .cin(1'b0));  // open: cout
  Adder #(.width(64)) adder_9 (.a(shifter_17_out), .b(shifter_18_out), .out(adder_9_out), .cin(1'b0));  // open: cout
  Adder #(.width(64)) adder_10 (.a(shifter_19_out), .b(shifter_20_out), .out(adder_10_out), .cin(1'b0));  // open: cout
  Adder #(.width(64)) adder_11 (.a(shifter_21_out), .b(shifter_22_out), .out(adder_11_out), .cin(1'b0));  // open: cout
  Adder #(.width(64)) adder_12 (.a(shifter_23_out), .b(shifter_24_out), .out(adder_12_out), .cin(1'b0));  // open: cout
  Adder #(.width(64)) adder_13 (.a(shifter_25_out), .b(shifter_26_out), .out(adder_13_out), .cin(1'b0));  // open: cout
  Adder #(.width(64)) adder_14 (.a(shifter_27_out), .b(shifter_28_out), .out(adder_14_out), .cin(1'b0));  // open: cout
  Adder #(.width(64)) adder_15 (.a(shifter_29_out), .b(shifter_30_out), .out(adder_15_out), .cin(1'b0));  // open: cout
  Adder #(.width(64)) adder_16 (.a(shifter_31_out), .b(shifter_32_out), .out(adder_16_out), .cin(1'b0));  // open: cout
  Adder #(.width(64)) adder_17 (.a(adder_1_out), .b(adder_2_out), .out(adder_17_out), .cin(1'b0));  // open: cout
  Adder #(.width(64)) adder_18 (.a(adder_3_out), .b(adder_4_out), .out(adder_18_out), .cin(1'b0));  // open: cout
  Adder #(.width(64)) adder_19 (.a(adder_5_out), .b(adder_6_out), .out(adder_19_out), .cin(1'b0));  // open: cout
  Adder #(.width(64)) adder_20 (.a(adder_7_out), .b(adder_8_out), .out(adder_20_out), .cin(1'b0));  // open: cout
  Adder #(.width(64)) adder_21 (.a(adder_9_out), .b(adder_10_out), .out(adder_21_out), .cin(1'b0));  // open: cout
  Adder #(.width(64)) adder_22 (.a(adder_11_out), .b(adder_12_out), .out(adder_22_out), .cin(1'b0));  // open: cout
  Adder #(.width(64)) adder_23 (.a(adder_13_out), .b(adder_14_out), .out(adder_23_out), .cin(1'b0));  // open: cout
  Adder #(.width(64)) adder_24 (.a(adder_15_out), .b(adder_16_out), .out(adder_24_out), .cin(1'b0));  // open: cout
  Adder #(.width(64)) adder_25 (.a(adder_17_out), .b(adder_18_out), .out(adder_25_out), .cin(1'b0));  // open: cout
  Adder #(.width(64)) adder_26 (.a(adder_19_out), .b(adder_20_out), .out(adder_26_out), .cin(1'b0));  // open: cout
  Adder #(.width(64)) adder_27 (.a(adder_21_out), .b(adder_22_out), .out(adder_27_out), .cin(1'b0));  // open: cout
  Adder #(.width(64)) adder_28 (.a(adder_23_out), .b(adder_24_out), .out(adder_28_out), .cin(1'b0));  // open: cout
  Adder #(.width(64)) adder_29 (.a(adder_25_out), .b(adder_26_out), .out(adder_29_out), .cin(1'b0));  // open: cout
  Adder #(.width(64)) adder_30 (.a(adder_27_out), .b(adder_28_out), .out(adder_30_out), .cin(1'b0));  // open: cout
  Adder #(.width(64)) adder_31 (.a(adder_29_out), .b(adder_30_out), .out({HIGH, LOW}), .cin(1'b0));  // open: cout

  // Other names for the same wires on the sheet: d1 = ALU_Ctrl[1]; d0 = ALU_Ctrl[0]; d2 = ALU_Ctrl[2]
endmodule
