// Logisim project HW1-403106681 (2).circ as structural Verilog: 1 circuit, main circuit main
module main (
  input  [31:0] A,
  input  [31:0] B,
  input  [2:0] ALU_Ctrl,
  output [31:0] Result_Lo,
  output [31:0] Result_Hi,
  output Z,
  output C,
  output V,
  output N
);

  wire ADD_S, ADD_U, and_3_out, and_4_out, and_5_out, and_6_out, and_10_out, Cout, MUL, NOP, NOP1, NOP2,
       NOP3, nor_1_out, not_2_out, not_3_out, not_4_out, not_5_out, not_6_out, not_7_out, not_8_out,
       not_9_out, not_10_out, not_11_out, not_12_out, SUB_S, SUB_U, xnor_1_out, xor_1_out, xor_2_out,
       xor_4_out;
  wire [30:0] or_2_out;
  wire [31:0] and_1_out, and_2_out, B_t, HIGH, LOW, multiplexer_3_out, multiplexer_4_out, multiplexer_5_out,
       multiplexer_6_out, multiplexer_7_out, multiplexer_8_out, multiplexer_9_out, multiplexer_10_out,
       multiplexer_11_out, multiplexer_12_out, multiplexer_13_out, multiplexer_14_out, multiplexer_15_out,
       multiplexer_16_out, multiplexer_17_out, multiplexer_18_out, multiplexer_19_out, multiplexer_20_out,
       multiplexer_21_out, multiplexer_22_out, multiplexer_23_out, multiplexer_24_out, multiplexer_25_out,
       multiplexer_26_out, multiplexer_27_out, multiplexer_28_out, multiplexer_29_out, multiplexer_30_out,
       multiplexer_31_out, multiplexer_32_out, multiplexer_33_out, multiplexer_34_out, multiplexer_35_out,
       not_1_out, S, xor_3_out;
  wire [63:0] adder_1_out, adder_2_out, adder_3_out, adder_4_out, adder_5_out, adder_6_out, adder_7_out,
       adder_8_out, adder_9_out, adder_10_out, adder_11_out, adder_12_out, adder_13_out, adder_14_out,
       adder_15_out, adder_16_out, adder_17_out, adder_18_out, adder_19_out, adder_20_out, adder_21_out,
       adder_22_out, adder_23_out, adder_24_out, adder_25_out, adder_26_out, adder_27_out, adder_28_out,
       adder_29_out, adder_30_out;

  assign not_1_out = ~B;  // NOT_Gate not_1, 32 bits wide
  Decoder #(.enable("false"), .select(3)) decoder_1 (
    .out0(ADD_U), .out1(ADD_S), .out2(SUB_U), .out3(SUB_S), .out4(MUL), .out5(NOP1), .out6(NOP2),
    .out7(NOP3), .sel(ALU_Ctrl));
  Multiplexer #(.width(32)) multiplexer_1 (.in0(B), .in1(not_1_out), .out(B_t), .sel(ALU_Ctrl[1]));
  or or_1 (NOP, NOP1, NOP2, NOP3);
  assign and_1_out = B_t & A;  // AND_Gate and_1, 32 bits wide
  xor xor_1 (xor_1_out, Cout, ALU_Ctrl[1]);
  xor xor_2 (xor_2_out, S[31], A[31]);
  assign xor_3_out = B_t ^ A;  // XOR_Gate xor_3, 32 bits wide
  assign {Cout, or_2_out} = and_1_out | and_2_out;  // OR_Gate or_2, 32 bits wide
  not not_2 (not_2_out, ALU_Ctrl[0]);
  not not_3 (not_3_out, ALU_Ctrl[2]);
  not not_4 (not_4_out, ALU_Ctrl[2]);
  xnor xnor_1 (xnor_1_out, A[31], B_t[31]);
  assign and_2_out = xor_3_out & {or_2_out, ALU_Ctrl[1]};  // AND_Gate and_2, 32 bits wide
  nor nor_1 (nor_1_out, S[0], S[1], S[2], S[3], S[4], S[5], S[6], S[7], S[8], S[9], S[10], S[11], S[12], S[13], S[14], S[15], S[16], S[17], S[18], S[19], S[20], S[21], S[22], S[23], S[24], S[25], S[26], S[27], S[28], S[29], S[30], S[31]);
  and and_3 (and_3_out, xor_1_out, not_2_out, not_3_out);
  not not_5 (not_5_out, NOP);
  and and_4 (and_4_out, xor_2_out, not_4_out, xnor_1_out);
  xor xor_4 (xor_4_out, and_5_out, S[31]);
  not not_6 (not_6_out, ALU_Ctrl[2]);
  assign S = {or_2_out, ALU_Ctrl[1]} ^ xor_3_out;  // XOR_Gate xor_5, 32 bits wide
  not not_7 (not_7_out, NOP);
  and and_5 (and_5_out, not_5_out, and_4_out);
  not not_8 (not_8_out, NOP);
  and and_6 (and_6_out, xor_4_out, ALU_Ctrl[0], not_6_out);
  not not_9 (not_9_out, NOP);
  not not_10 (not_10_out, C);
  and and_7 (C, not_7_out, and_3_out);
  and and_8 (N, not_8_out, and_6_out);
  and and_9 (Z, not_9_out, not_10_out, nor_1_out);
  Multiplexer multiplexer_2 (.in0(and_5_out), .in1(C), .out(V), .sel(and_10_out));
  and and_10 (and_10_out, not_11_out, not_12_out);
  not not_11 (not_11_out, ALU_Ctrl[2]);
  not not_12 (not_12_out, ALU_Ctrl[0]);
  Multiplexer #(.width(32)) multiplexer_3 (.in0({32{1'b0}}), .in1(A), .out(multiplexer_3_out), .sel(B_t[0]));
  Multiplexer #(.width(32)) multiplexer_4 (.in0({32{1'b0}}), .in1(A), .out(multiplexer_4_out), .sel(B_t[1]));
  Multiplexer #(.width(32)) multiplexer_5 (.in0({32{1'b0}}), .in1(A), .out(multiplexer_5_out), .sel(B_t[2]));
  Multiplexer #(.width(32)) multiplexer_6 (.in0({32{1'b0}}), .in1(A), .out(multiplexer_6_out), .sel(B_t[3]));
  Multiplexer #(.width(32)) multiplexer_7 (.in0({32{1'b0}}), .in1(A), .out(multiplexer_7_out), .sel(B_t[4]));
  Multiplexer #(.width(32)) multiplexer_8 (.in0({32{1'b0}}), .in1(A), .out(multiplexer_8_out), .sel(B_t[5]));
  Multiplexer #(.width(32)) multiplexer_9 (.in0({32{1'b0}}), .in1(A), .out(multiplexer_9_out), .sel(B_t[6]));
  Multiplexer #(.width(32)) multiplexer_10 (.in0({32{1'b0}}), .in1(A), .out(multiplexer_10_out), .sel(B_t[7]));
  Multiplexer #(.width(32)) multiplexer_11 (.in0({32{1'b0}}), .in1(A), .out(multiplexer_11_out), .sel(B_t[8]));
  Multiplexer #(.width(32)) multiplexer_12 (.in0({32{1'b0}}), .in1(A), .out(multiplexer_12_out), .sel(B_t[9]));
  Multiplexer #(.width(32)) multiplexer_13 (.in0({32{1'b0}}), .in1(A), .out(multiplexer_13_out), .sel(B_t[10]));
  Multiplexer #(.width(32)) multiplexer_14 (.in0({32{1'b0}}), .in1(A), .out(multiplexer_14_out), .sel(B_t[11]));
  Multiplexer #(.width(32)) multiplexer_15 (.in0({32{1'b0}}), .in1(A), .out(multiplexer_15_out), .sel(B_t[12]));
  Multiplexer #(.width(32)) multiplexer_16 (.in0({32{1'b0}}), .in1(A), .out(multiplexer_16_out), .sel(B_t[13]));
  Multiplexer #(.width(32)) multiplexer_17 (.in0({32{1'b0}}), .in1(A), .out(multiplexer_17_out), .sel(B_t[14]));
  Multiplexer #(.width(32)) multiplexer_18 (.in0({32{1'b0}}), .in1(A), .out(multiplexer_18_out), .sel(B_t[15]));
  Multiplexer #(.width(32)) multiplexer_19 (.in0({32{1'b0}}), .in1(A), .out(multiplexer_19_out), .sel(B_t[16]));
  Multiplexer #(.width(32)) multiplexer_20 (.in0({32{1'b0}}), .in1(A), .out(multiplexer_20_out), .sel(B_t[17]));
  Multiplexer #(.width(32)) multiplexer_21 (.in0({32{1'b0}}), .in1(A), .out(multiplexer_21_out), .sel(B_t[18]));
  Multiplexer #(.width(32)) multiplexer_22 (.in0({32{1'b0}}), .in1(A), .out(multiplexer_22_out), .sel(B_t[19]));
  Multiplexer #(.width(32)) multiplexer_23 (.in0({32{1'b0}}), .in1(A), .out(multiplexer_23_out), .sel(B_t[20]));
  Multiplexer #(.width(32)) multiplexer_24 (.in0({32{1'b0}}), .in1(A), .out(multiplexer_24_out), .sel(B_t[21]));
  Multiplexer #(.width(32)) multiplexer_25 (.in0({32{1'b0}}), .in1(A), .out(multiplexer_25_out), .sel(B_t[22]));
  Multiplexer #(.width(32)) multiplexer_26 (.in0({32{1'b0}}), .in1(A), .out(multiplexer_26_out), .sel(B_t[23]));
  Multiplexer #(.width(32)) multiplexer_27 (.in0({32{1'b0}}), .in1(A), .out(multiplexer_27_out), .sel(B_t[24]));
  Multiplexer #(.width(32)) multiplexer_28 (.in0({32{1'b0}}), .in1(A), .out(multiplexer_28_out), .sel(B_t[25]));
  Multiplexer #(.width(32)) multiplexer_29 (.in0({32{1'b0}}), .in1(A), .out(multiplexer_29_out), .sel(B_t[26]));
  Multiplexer #(.width(32)) multiplexer_30 (.in0({32{1'b0}}), .in1(A), .out(multiplexer_30_out), .sel(B_t[27]));
  Multiplexer #(.width(32)) multiplexer_31 (.in0({32{1'b0}}), .in1(A), .out(multiplexer_31_out), .sel(B_t[28]));
  Multiplexer #(.width(32)) multiplexer_32 (.in0({32{1'b0}}), .in1(A), .out(multiplexer_32_out), .sel(B_t[29]));
  Multiplexer #(.width(32)) multiplexer_33 (.in0({32{1'b0}}), .in1(A), .out(multiplexer_33_out), .sel(B_t[30]));
  Multiplexer #(.width(32)) multiplexer_34 (.in0({32{1'b0}}), .in1(A), .out(multiplexer_34_out), .sel(B_t[31]));
  Adder #(.width(64)) adder_1 (
    .a({{32{1'b0}}, multiplexer_3_out}), .b({{31{1'b0}}, multiplexer_4_out, 1'b0}), .out(adder_1_out),
    .cin(1'b0));  // open: cout
  Adder #(.width(64)) adder_2 (
    .a({{30{1'b0}}, multiplexer_5_out, 2'b00}), .b({{29{1'b0}}, multiplexer_6_out, 3'b000}),
    .out(adder_2_out), .cin(1'b0));  // open: cout
  Adder #(.width(64)) adder_3 (
    .a({{28{1'b0}}, multiplexer_7_out, 4'b0000}), .b({{27{1'b0}}, multiplexer_8_out, {5{1'b0}}}),
    .out(adder_3_out), .cin(1'b0));  // open: cout
  Adder #(.width(64)) adder_4 (
    .a({{26{1'b0}}, multiplexer_9_out, {6{1'b0}}}), .b({{25{1'b0}}, multiplexer_10_out, {7{1'b0}}}),
    .out(adder_4_out), .cin(1'b0));  // open: cout
  Adder #(.width(64)) adder_5 (
    .a({{24{1'b0}}, multiplexer_11_out, {8{1'b0}}}), .b({{23{1'b0}}, multiplexer_12_out, {9{1'b0}}}),
    .out(adder_5_out), .cin(1'b0));  // open: cout
  Adder #(.width(64)) adder_6 (
    .a({{22{1'b0}}, multiplexer_13_out, {10{1'b0}}}), .b({{21{1'b0}}, multiplexer_14_out, {11{1'b0}}}),
    .out(adder_6_out), .cin(1'b0));  // open: cout
  Adder #(.width(64)) adder_7 (
    .a({{20{1'b0}}, multiplexer_15_out, {12{1'b0}}}), .b({{19{1'b0}}, multiplexer_16_out, {13{1'b0}}}),
    .out(adder_7_out), .cin(1'b0));  // open: cout
  Adder #(.width(64)) adder_8 (
    .a({{18{1'b0}}, multiplexer_17_out, {14{1'b0}}}), .b({{17{1'b0}}, multiplexer_18_out, {15{1'b0}}}),
    .out(adder_8_out), .cin(1'b0));  // open: cout
  Adder #(.width(64)) adder_9 (
    .a({{16{1'b0}}, multiplexer_19_out, {16{1'b0}}}), .b({{15{1'b0}}, multiplexer_20_out, {17{1'b0}}}),
    .out(adder_9_out), .cin(1'b0));  // open: cout
  Adder #(.width(64)) adder_10 (
    .a({{14{1'b0}}, multiplexer_21_out, {18{1'b0}}}), .b({{13{1'b0}}, multiplexer_22_out, {19{1'b0}}}),
    .out(adder_10_out), .cin(1'b0));  // open: cout
  Adder #(.width(64)) adder_11 (
    .a({{12{1'b0}}, multiplexer_23_out, {20{1'b0}}}), .b({{11{1'b0}}, multiplexer_24_out, {21{1'b0}}}),
    .out(adder_11_out), .cin(1'b0));  // open: cout
  Adder #(.width(64)) adder_12 (
    .a({{10{1'b0}}, multiplexer_25_out, {22{1'b0}}}), .b({{9{1'b0}}, multiplexer_26_out, {23{1'b0}}}),
    .out(adder_12_out), .cin(1'b0));  // open: cout
  Adder #(.width(64)) adder_13 (
    .a({{8{1'b0}}, multiplexer_27_out, {24{1'b0}}}), .b({{7{1'b0}}, multiplexer_28_out, {25{1'b0}}}),
    .out(adder_13_out), .cin(1'b0));  // open: cout
  Adder #(.width(64)) adder_14 (
    .a({{6{1'b0}}, multiplexer_29_out, {26{1'b0}}}), .b({{5{1'b0}}, multiplexer_30_out, {27{1'b0}}}),
    .out(adder_14_out), .cin(1'b0));  // open: cout
  Adder #(.width(64)) adder_15 (
    .a({4'b0000, multiplexer_31_out, {28{1'b0}}}), .b({3'b000, multiplexer_32_out, {29{1'b0}}}),
    .out(adder_15_out), .cin(1'b0));  // open: cout
  Adder #(.width(64)) adder_16 (
    .a({2'b00, multiplexer_33_out, {30{1'b0}}}), .b({1'b0, multiplexer_34_out, {31{1'b0}}}),
    .out(adder_16_out), .cin(1'b0));  // open: cout
  Adder #(.width(64)) adder_17 (.a(adder_1_out), .b(adder_2_out), .out(adder_17_out), .cin(1'b0));  // open: cout
  Adder #(.width(64)) adder_18 (.a(adder_3_out), .b(adder_4_out), .out(adder_18_out), .cin(1'b0));  // open: cout
  Adder #(.width(64)) adder_19 (.a(adder_5_out), .b(adder_6_out), .out(adder_19_out), .cin(1'b0));  // open: cout
  Adder #(.width(64)) adder_20 (.a(adder_7_out), .b(adder_8_out), .out(adder_20_out), .cin(1'b0));  // open: cout
  Adder #(.width(64)) adder_21 (.a(adder_9_out), .b(adder_10_out), .out(adder_21_out), .cin(1'b0));  // open: cout
  Adder #(.width(64)) adder_22 (.a(adder_11_out), .b(adder_12_out), .out(adder_22_out), .cin(1'b0));  // open: cout
  Adder #(.width(64)) adder_23 (.a(adder_13_out), .b(adder_14_out), .out(adder_23_out), .cin(1'b0));  // open: cout
  Adder #(.width(64)) adder_24 (.a(adder_15_out), .b(adder_16_out), .out(adder_24_out), .cin(1'b0));  // open: cout
  Multiplexer #(.width(32)) multiplexer_35 (.in0(S), .in1(LOW), .out(multiplexer_35_out), .sel(ALU_Ctrl[2]));
  Adder #(.width(64)) adder_25 (.a(adder_17_out), .b(adder_18_out), .out(adder_25_out), .cin(1'b0));  // open: cout
  Adder #(.width(64)) adder_26 (.a(adder_19_out), .b(adder_20_out), .out(adder_26_out), .cin(1'b0));  // open: cout
  Adder #(.width(64)) adder_27 (.a(adder_21_out), .b(adder_22_out), .out(adder_27_out), .cin(1'b0));  // open: cout
  Adder #(.width(64)) adder_28 (.a(adder_23_out), .b(adder_24_out), .out(adder_28_out), .cin(1'b0));  // open: cout
  Multiplexer #(.width(32)) multiplexer_36 (.in0(multiplexer_35_out), .in1({32{1'b0}}), .out(Result_Lo), .sel(NOP));
  Multiplexer #(.width(32)) multiplexer_37 (.in0({32{1'b0}}), .in1(HIGH), .out(Result_Hi), .sel(MUL));
  Adder #(.width(64)) adder_29 (.a(adder_25_out), .b(adder_26_out), .out(adder_29_out), .cin(1'b0));  // open: cout
  Adder #(.width(64)) adder_30 (.a(adder_27_out), .b(adder_28_out), .out(adder_30_out), .cin(1'b0));  // open: cout
  Adder #(.width(64)) adder_31 (.a(adder_29_out), .b(adder_30_out), .out({HIGH, LOW}), .cin(1'b0));  // open: cout

  // Other names for the same wires on the sheet: d1 = ALU_Ctrl[1]; d0 = ALU_Ctrl[0]; d2 = ALU_Ctrl[2]

  // Notes on the sheet:
  //   Input
  //   32-bit full adder/subtractor
  //   Flags
  //   32-bit Multiplier
  //   Output
endmodule
