// Logisim project HW2C-403106681.circ as structural Verilog: 3 circuits, main circuit main
module main (
  input  [31:0] Data,
  input  [1:0] Count_Op,
  output [5:0] Count
);

  wire [31:0] bit_reversal_1_outp, Data0, multiplexer_2_out, not_1_out;

  Multiplexer #(.width(32)) multiplexer_1 (.in0(Data), .in1(not_1_out), .out(Data0), .sel(Count_Op[0]));
  assign not_1_out = ~Data;  // NOT_Gate not_1, 32 bits wide
  Bit_Reversal bit_reversal_1 (.INP(Data0), .OUTP(bit_reversal_1_outp));
  Multiplexer #(.width(32)) multiplexer_2 (
    .in0(Data0), .in1(bit_reversal_1_outp), .out(multiplexer_2_out), .sel(Count_Op[1]));
  CTZ ctz_1 (.A(multiplexer_2_out), .CTZ_out(Count));

  // Other names for the same wires on the sheet: d0 = Count_Op[0]; d1 = Count_Op[1]
endmodule

module CTZ (
  input  [31:0] A,
  output [5:0] CTZ_out
);

  wire C0, C1, C2, C3, C4, not_7_out, or_1_out, or_2_out, or_3_out, or_4_out, or_5_out;
  wire [1:0] STAGE1;
  wire [3:0] STAGE2;
  wire [7:0] STAGE3;
  wire [15:0] STAGE4;

  not not_1 (C0, STAGE1[0]);
  or or_1 (or_1_out, STAGE4[0], STAGE4[1], STAGE4[2], STAGE4[3], STAGE4[4], STAGE4[5], STAGE4[6], STAGE4[7]);
  or or_2 (or_2_out, STAGE3[0], STAGE3[1], STAGE3[2], STAGE3[3]);
  or or_3 (or_3_out, STAGE2[0], STAGE2[1]);
  or or_4 (or_4_out, A[0], A[1], A[2], A[3], A[4], A[5], A[6], A[7], A[8], A[9], A[10], A[11], A[12], A[13], A[14], A[15], A[16], A[17], A[18], A[19], A[20], A[21], A[22], A[23], A[24], A[25], A[26], A[27], A[28], A[29], A[30], A[31]);
  not not_2 (CTZ_out[5], or_4_out);
  or or_5 (or_5_out, A[0], A[1], A[2], A[3], A[4], A[5], A[6], A[7], A[8], A[9], A[10], A[11], A[12], A[13], A[14], A[15]);
  not not_3 (C4, or_5_out);
  not not_4 (C3, or_1_out);
  not not_5 (C2, or_2_out);
  not not_6 (C1, or_3_out);
  Multiplexer #(.width(16)) multiplexer_1 (.in0(A[15:0]), .in1(A[31:16]), .out(STAGE4), .sel(C4));
  Multiplexer #(.width(8)) multiplexer_2 (.in0(STAGE4[7:0]), .in1(STAGE4[15:8]), .out(STAGE3), .sel(C3));
  Multiplexer #(.width(4)) multiplexer_3 (.in0(STAGE3[3:0]), .in1(STAGE3[7:4]), .out(STAGE2), .sel(C2));
  Multiplexer #(.width(2)) multiplexer_4 (.in0(STAGE2[1:0]), .in1(STAGE2[3:2]), .out(STAGE1), .sel(C1));
  not not_7 (not_7_out, CTZ_out[5]);
  and and_1 (CTZ_out[0], C0, not_7_out);
  and and_2 (CTZ_out[1], C1, not_7_out);
  and and_3 (CTZ_out[2], C2, not_7_out);
  and and_4 (CTZ_out[3], C3, not_7_out);
  and and_5 (CTZ_out[4], C4, not_7_out);

  // Other names for the same wires on the sheet: C5 = CTZ_out[5]
endmodule

module Bit_Reversal (
  input  [31:0] INP,
  output [31:0] OUTP
);


  assign OUTP = {INP[0], INP[1], INP[2], INP[3], INP[4], INP[5], INP[6], INP[7], INP[8], INP[9], INP[10], INP[11], INP[12], INP[13], INP[14], INP[15], INP[16], INP[17], INP[18], INP[19], INP[20], INP[21], INP[22], INP[23], INP[24], INP[25], INP[26], INP[27], INP[28], INP[29], INP[30], INP[31]};
endmodule
