// Logisim project HW2S-403106681.circ as structural Verilog: 3 circuits, main circuit main
module main (
  input  [31:0] Data,
  input  [4:0] Shift_Amt,
  input  [1:0] Shift_Op,
  output [31:0] Result
);

  wire nor_1_out, undriven, undriven_2;
  wire [31:0] bit_reversal_1_outp, bit_reversal_2_outp, multiplexer_1_out, shrl_1_outpt;

  nor nor_1 (nor_1_out, Shift_Op[0], Shift_Op[1]);
  Multiplexer #(.width(32)) multiplexer_1 (
    .in0(Data), .in1(bit_reversal_1_outp), .out(multiplexer_1_out), .sel(undriven));
  Bit_Reversal bit_reversal_1 (.INP(Data), .OUTP(bit_reversal_1_outp));
  SHRL shrl_1 (
    .Data(multiplexer_1_out), .Shift_Amt(Shift_Amt), .SHRA(Shift_Op[1]), .Data_31(Data[31]),
    .OUTPT(shrl_1_outpt));
  Multiplexer #(.width(32)) multiplexer_2 (
    .in0(shrl_1_outpt), .in1(bit_reversal_2_outp), .out(Result), .sel(undriven_2));
  Bit_Reversal bit_reversal_2 (.INP(shrl_1_outpt), .OUTP(bit_reversal_2_outp));

  // Other names for the same wires on the sheet: d0 = Shift_Op[0]; d1 = Shift_Op[1]
endmodule

module SHRL (
  input  [31:0] Data,
  input  [4:0] Shift_Amt,
  input  SHRA,
  input  Data_31,
  output [31:0] OUTPT
);

  wire fill;
  wire [31:0] A0, A1, A2, A3;

  Multiplexer multiplexer_1 (.in0(1'b0), .in1(Data_31), .out(fill), .sel(SHRA));
  Multiplexer #(.width(32)) multiplexer_2 (.in0(Data), .in1({fill, Data[31:1]}), .out(A0), .sel(Shift_Amt[0]));
  Multiplexer #(.width(32)) multiplexer_3 (.in0(A0), .in1({{2{fill}}, A0[31:2]}), .out(A1), .sel(Shift_Amt[1]));
  Multiplexer #(.width(32)) multiplexer_4 (.in0(A1), .in1({{4{fill}}, A1[31:4]}), .out(A2), .sel(Shift_Amt[2]));
  Multiplexer #(.width(32)) multiplexer_5 (.in0(A2), .in1({{8{fill}}, A2[31:8]}), .out(A3), .sel(Shift_Amt[3]));
  Multiplexer #(.width(32)) multiplexer_6 (.in0(A3), .in1({{16{fill}}, A3[31:16]}), .out(OUTPT), .sel(Shift_Amt[4]));

  // Other names for the same wires on the sheet: A[31:0] = Data; b0 = Shift_Amt[0]; b1 = Shift_Amt[1];
  //   b2 = Shift_Amt[2]; b3 = Shift_Amt[3]; b4 = Shift_Amt[4]
endmodule

module Bit_Reversal (
  input  [31:0] INP,
  output [31:0] OUTP
);


  assign OUTP = {INP[0], INP[1], INP[2], INP[3], INP[4], INP[5], INP[6], INP[7], INP[8], INP[9], INP[10], INP[11], INP[12], INP[13], INP[14], INP[15], INP[16], INP[17], INP[18], INP[19], INP[20], INP[21], INP[22], INP[23], INP[24], INP[25], INP[26], INP[27], INP[28], INP[29], INP[30], INP[31]};
endmodule
