// Logisim project HW3-403106681.circ as structural Verilog: 6 circuits, main circuit main
module main (
  input  [31:0] A,
  input  [31:0] B,
  input  Start,
  input  Rst,
  input  Clk,
  input  Divide,
  output [31:0] Result_Lo,
  output [31:0] Result_Hi,
  output Done
);

  wire div_1_done, mul_1_done;
  wire [31:0] div_1_result_hi, div_1_result_lo, mul_1_result_hi, mul_1_result_lo;

  MUL mul_1 (
    .A(A), .B(B), .Start(Start), .Rst(Rst), .Clk(Clk), .Result_Lo(mul_1_result_lo),
    .Result_Hi(mul_1_result_hi), .Done(mul_1_done));
  DIV div_1 (
    .A(A), .B(B), .Start(Start), .Rst(Rst), .Clk(Clk), .Result_Lo(div_1_result_lo),
    .Result_Hi(div_1_result_hi), .Done(div_1_done));
  Multiplexer multiplexer_1 (.in0(mul_1_done), .in1(div_1_done), .out(Done), .sel(Divide));
  Multiplexer #(.width(64)) multiplexer_2 (
    .in0({mul_1_result_hi, mul_1_result_lo}), .in1({div_1_result_hi, div_1_result_lo}),
    .out({Result_Hi, Result_Lo}), .sel(Divide));
endmodule

module CU (
  input  Clk,
  input  Rst,
  input  Start,
  input  Z,
  output INIT,
  output LOAD,
  output CALC
);

  wire and_1_out, and_2_out, and_4_out, D_CALC, D_INIT, D_LOAD, not_1_out, not_2_out;

  D_Flip_Flop d_ff_1 (.D(D_INIT), .clk(Clk), .Q(INIT), .preset(Rst));  // open: Qn, reset
  D_Flip_Flop d_ff_2 (.D(D_LOAD), .clk(Clk), .Q(LOAD), .reset(Rst));  // open: Qn, preset
  D_Flip_Flop d_ff_3 (.D(D_CALC), .clk(Clk), .Q(CALC), .reset(Rst));  // open: Qn, preset
  not not_1 (not_1_out, Start);
  and and_1 (and_1_out, CALC, Z);
  not not_2 (not_2_out, Z);
  and and_2 (and_2_out, not_2_out, CALC);
  and and_3 (D_LOAD, INIT, Start);
  and and_4 (and_4_out, INIT, not_1_out);
  or or_1 (D_INIT, and_4_out, and_1_out);
  or or_2 (D_CALC, and_2_out, LOAD);
endmodule

module SHR (
  input  [63:0] P,
  output [63:0] OUTP
);


  assign OUTP = {1'b0, P[63:1]};
endmodule

module Cnt (
  input  [4:0] D_Count,
  input  dec_Count,
  input  Rst,
  input  ld_Count,
  input  Clk,
  output [4:0] Q_Count
);

  wire or_1_out;
  wire [4:0] adder_1_out, multiplexer_1_out;

  Multiplexer #(.width(5)) multiplexer_1 (.in0(D_Count), .in1(adder_1_out), .out(multiplexer_1_out), .sel(dec_Count));
  or or_1 (or_1_out, dec_Count, ld_Count);
  Register #(.width(5)) register_1 (.D(multiplexer_1_out), .en(or_1_out), .clk(Clk), .Q(Q_Count), .clr(Rst));
  Adder #(.width(5)) adder_1 (.a(Q_Count), .b({5{1'b1}}), .out(adder_1_out), .cin(1'b0));  // open: cout
endmodule

module MUL (
  input  [31:0] A,
  input  [31:0] B,
  input  Start,
  input  Rst,
  input  Clk,
  output [31:0] Result_Lo,
  output [31:0] Result_Hi,
  output Done
);

  wire and_3_out, CALC, INIT, ld_Count, ld_P, not_1_out, Z;
  wire [1:0] and_2_out;
  wire [4:0] cnt_1_q_count;
  wire [31:0] adder_1_out;
  wire [63:0] DP, shr_1_outp;
  wire [63:63] adder_1_cout;

  Adder #(.width(32)) adder_1 (.a(Result_Hi), .b(A), .out(adder_1_out), .cin(1'b0), .cout(adder_1_cout[63]));
  or or_1 (ld_P, ld_Count, CALC);
  SHR shr_1 (.P({Result_Hi, Result_Lo}), .OUTP(shr_1_outp));
  and and_1 (and_2_out[1], not_1_out, CALC);
  not not_1 (not_1_out, Result_Lo[0]);
  Multiplexer #(.select(2), .width(64)) multiplexer_1 (
    .in0({{32{1'b0}}, B}), .in1({adder_1_cout[63], adder_1_out, Result_Lo[31:1]}), .in2(shr_1_outp),
    .in3({Result_Hi, Result_Lo}), .out(DP), .sel(and_2_out));
  and and_2 (and_2_out[0], CALC, Result_Lo[0]);
  Clock #(.phaseOffset(1)) Clk_test ();  // open: out
  Register #(.width(32)) RA (.D(A), .en(ld_Count), .clk(Clk), .clr(Rst));  // open: Q
  Register #(.width(64)) P (.D(DP), .en(ld_P), .clk(Clk), .Q({Result_Hi, Result_Lo}), .clr(Rst));
  Cnt cnt_1 (.D_Count({5{1'b1}}), .dec_Count(CALC), .Rst(Rst), .ld_Count(ld_Count), .Clk(Clk), .Q_Count(cnt_1_q_count));
  CU cu_1 (.Clk(Clk), .Rst(Rst), .Start(Start), .Z(Z), .INIT(INIT), .LOAD(ld_Count), .CALC(CALC));
  nor nor_1 (Z, cnt_1_q_count[0], cnt_1_q_count[1], cnt_1_q_count[2], cnt_1_q_count[3], cnt_1_q_count[4]);
  and and_3 (and_3_out, Z, CALC);
  S_R_Flip_Flop s_r_ff_1 (.S(and_3_out), .R(Start), .clk(Clk), .Q(Done));  // open: reset, Qn, preset

  // Other names for the same wires on the sheet: P[63:0] = {Result_Hi, Result_Lo}; P0 = Result_Lo[0];
  //   dec_Count = CALC; ld_RA = ld_Count; LOAD = ld_Count
endmodule

module DIV (
  input  [31:0] A,
  input  [31:0] B,
  input  Start,
  input  Rst,
  input  Clk,
  output [31:0] Result_Lo,
  output [31:0] Result_Hi,
  output Done
);

  wire adder_1_cout, and_3_out, CALC, INIT, ld_Count, ld_R, not_2_out, Z;
  wire [1:0] and_2_out;
  wire [4:0] cnt_1_q_count;
  wire [31:0] adder_1_out, not_1_out;
  wire [63:0] DR;

  or or_1 (ld_R, ld_Count, CALC);
  assign not_1_out = ~B;  // NOT_Gate not_1, 32 bits wide
  Adder #(.width(32)) adder_1 (
    .a({Result_Hi[30:0], Result_Lo[31]}), .b(not_1_out), .out(adder_1_out), .cin(1'b1), .cout(adder_1_cout));
  and and_1 (and_2_out[1], not_2_out, CALC);
  not not_2 (not_2_out, adder_1_cout);
  Clock #(.phaseOffset(1)) Clk_test ();  // open: out
  Multiplexer #(.select(2), .width(64)) multiplexer_1 (
    .in0({{32{1'b0}}, A}), .in1({adder_1_out, Result_Lo[30:0], 1'b1}),
    .in2({Result_Hi[30:0], Result_Lo, 1'b0}), .in3({Result_Hi, Result_Lo}), .out(DR), .sel(and_2_out));
  and and_2 (and_2_out[0], CALC, adder_1_cout);
  Register #(.width(32)) RB (.D(B), .en(ld_Count), .clk(Clk), .clr(Rst));  // open: Q
  Register #(.width(64)) R (.D(DR), .en(ld_R), .clk(Clk), .Q({Result_Hi, Result_Lo}), .clr(Rst));
  Cnt cnt_1 (.D_Count({5{1'b1}}), .dec_Count(CALC), .Rst(Rst), .ld_Count(ld_Count), .Clk(Clk), .Q_Count(cnt_1_q_count));
  CU cu_1 (.Clk(Clk), .Rst(Rst), .Start(Start), .Z(Z), .INIT(INIT), .LOAD(ld_Count), .CALC(CALC));
  nor nor_1 (Z, cnt_1_q_count[0], cnt_1_q_count[1], cnt_1_q_count[2], cnt_1_q_count[3], cnt_1_q_count[4]);
  and and_3 (and_3_out, Z, CALC);
  S_R_Flip_Flop s_r_ff_1 (.S(and_3_out), .R(Start), .clk(Clk), .Q(Done));  // open: reset, Qn, preset

  // Other names for the same wires on the sheet: R[63:0] = {Result_Hi, Result_Lo}; dec_Count = CALC; ld_RB = ld_Count;
  //   LOAD = ld_Count
endmodule
