// Logisim project HW4-403106681.circ as structural Verilog: 7 circuits, main circuit main
module main (
  input  [31:0] A,
  input  [31:0] B,
  input  Clk,
  input  Rst,
  input  Start,
  input  Sub,
  output [31:0] Result,
  output Done
);

  wire A_smaller, ADD, adder_1_cout, adder_3_cout, adder_4_cout, ALIGN, ALU_Carry, ALU_Op, and_1_out,
       and_2_out, and_3_out, and_4_out, and_5_out, and_6_out, and_7_out, and_8_out, Check_Done, CMP,
       comparator_1_eq, comparator_1_gt, denorm_A, denorm_B, DONE_t, Exception, G, G_Align, INIT, Is_Eq,
       Is_Not_Zero, Is_Ovf, LOAD, MA_Less, multiplexer_11_out, NORM, not_3_out, not_4_out, not_5_out,
       not_7_out, not_8_out, not_10_out, not_17_out, not_18_out, or_2_out, or_4_out, or_5_out, or_6_out,
       or_7_out, or_8_out, or_9_out, or_10_out, R_Align, ROUND, Round_Up, Rsub, S_Align, S_L, SA, SB,
       Shift_Ovf, Sign_Final;
  wire [1:0] Mantis_Norm;
  wire [4:0] Left_Shift_Amt, multiplexer_12_out, not_15_out, pe_1_o1;
  wire [7:0] adder_3_out, adder_5_out, adder_7_out, EA, EB, EXP_Norm, Exponent_L, multiplexer_3_out,
       multiplexer_4_out, multiplexer_9_out, multiplexer_10_out, multiplexer_13_out, multiplexer_14_out,
       not_9_out, not_11_out, not_16_out, Shift_Amt;
  wire [22:0] FA, FB, Final_Fraction;
  wire [23:0] adder_2_out, Fraction_Norm, Mantis_L, Mantis_S, Mantis_S_Aligned, multiplexer_6_out,
       multiplexer_7_out, not_1_out;
  wire [23:23] Mantis_A, Mantis_B, Mantis_Rounded;
  wire [26:0] adder_4_out, bit_reversal_1_outp, bit_reversal_2_outp, Mantis_Sum, multiplexer_5_out,
       multiplexer_15_out, not_6_out, shift_27_1_outp, shift_27_2_outp;
  wire [47:0] barrel_shifter_1_outp;

  and and_1 (and_1_out, Is_Eq, MA_Less);
  Multiplexer multiplexer_1 (.in0(1'b1), .in1(1'b0), .out(Mantis_A[23]), .sel(denorm_A));
  Multiplexer multiplexer_2 (.in0(1'b1), .in1(1'b0), .out(Mantis_B[23]), .sel(denorm_B));
  Adder #(.width(24)) adder_1 (.a({Mantis_A[23], FA}), .b(not_1_out), .cin(1'b1), .cout(adder_1_cout));  // open: out
  assign not_1_out = ~{Mantis_B[23], FB};  // NOT_Gate not_1, 24 bits wide
  not not_2 (MA_Less, adder_1_cout);
  Multiplexer #(.width(8)) multiplexer_3 (.in0(EA), .in1(8'h1), .out(multiplexer_3_out), .sel(denorm_A));
  Multiplexer #(.width(8)) multiplexer_4 (.in0(EB), .in1(8'h1), .out(multiplexer_4_out), .sel(denorm_B));
  or or_1 (A_smaller, not_10_out, and_1_out);
  not not_3 (not_3_out, SA);
  not not_4 (not_4_out, SB);
  not not_5 (not_5_out, Rsub);
  Adder #(.width(24)) adder_2 (.a(Fraction_Norm), .b({24{1'b0}}), .out(adder_2_out), .cin(Round_Up), .cout(Check_Done));
  Clock clock_1 ();  // open: out
  and and_2 (and_2_out, Rsub, A_smaller);
  Register #(.width(1)) register_1 (.D(or_2_out), .en(CMP), .clk(Clk), .Q(ALU_Op));  // open: clr
  and and_3 (and_3_out, not_3_out, not_4_out, Rsub);
  and and_4 (and_4_out, not_3_out, SB, not_5_out);
  and and_5 (and_5_out, SA, not_4_out, not_5_out);
  and and_6 (and_6_out, SA, SB, Rsub);
  Multiplexer #(.width(27)) multiplexer_5 (
    .in0({Mantis_S_Aligned, G_Align, R_Align, S_Align}), .in1(not_6_out), .out(multiplexer_5_out),
    .sel(ALU_Op));
  assign not_6_out = ~{Mantis_S_Aligned, G_Align, R_Align, S_Align};  // NOT_Gate not_6, 27 bits wide
  Register #(.width(24)) register_2 (
    .D(adder_2_out), .en(ROUND), .clk(Clk), .Q({Mantis_Rounded[23], Final_Fraction}));  // open: clr
  not not_7 (not_7_out, S_L);
  not not_8 (not_8_out, and_2_out);
  Adder adder_3 (.a(multiplexer_3_out), .b(not_9_out), .out(adder_3_out), .cin(1'b1), .cout(adder_3_cout));
  assign not_9_out = ~multiplexer_4_out;  // NOT_Gate not_9, 8 bits wide
  not not_10 (not_10_out, adder_3_cout);
  Multiplexer #(.width(24)) multiplexer_6 (
    .in0({Mantis_B[23], FB}), .in1({Mantis_A[23], FA}), .out(multiplexer_6_out), .sel(A_smaller));
  Multiplexer #(.width(24)) multiplexer_7 (
    .in0({Mantis_A[23], FA}), .in1({Mantis_B[23], FB}), .out(multiplexer_7_out), .sel(A_smaller));
  or or_2 (or_2_out, and_3_out, and_4_out, and_5_out, and_6_out);
  and and_7 (and_7_out, not_7_out, and_2_out);
  and and_8 (and_8_out, S_L, not_8_out);
  Multiplexer #(.width(32)) multiplexer_8 (
    .in0({32{1'b0}}), .in1({Sign_Final, EXP_Norm, Final_Fraction}), .out(Result), .sel(Is_Not_Zero));
  or or_3 (Sign_Final, and_7_out, and_8_out);
  Register #(.width(32)) RA (.D(A), .en(Start), .clk(Clk), .Q({SA, EA, FA}));  // open: clr
  Register #(.width(32)) RB (.D(B), .en(Start), .clk(Clk), .Q({SB, EB, FB}));  // open: clr
  Register #(.width(1)) u_Rsub (.D(Sub), .en(Start), .clk(Clk), .Q(Rsub));  // open: clr
  or or_4 (or_4_out, adder_3_out[0], adder_3_out[1], adder_3_out[2], adder_3_out[3], adder_3_out[4], adder_3_out[5], adder_3_out[6], adder_3_out[7]);
  assign not_11_out = ~adder_3_out;  // NOT_Gate not_11, 8 bits wide
  Register register_3 (.D(multiplexer_9_out), .en(CMP), .clk(Clk), .Q(Exponent_L));  // open: clr
  Multiplexer #(.width(8)) multiplexer_9 (
    .in0(multiplexer_3_out), .in1(multiplexer_4_out), .out(multiplexer_9_out), .sel(A_smaller));
  Register #(.width(24)) register_4 (.D(multiplexer_6_out), .en(CMP), .clk(Clk), .Q(Mantis_S));  // open: clr
  Register #(.width(24)) register_5 (.D(multiplexer_7_out), .en(CMP), .clk(Clk), .Q(Mantis_L));  // open: clr
  Adder #(.width(27)) adder_4 (
    .a({Mantis_L, 3'b000}), .b(multiplexer_5_out), .out(adder_4_out), .cin(ALU_Op), .cout(adder_4_cout));
  not not_12 (Is_Eq, or_4_out);
  Adder adder_5 (.a(not_11_out), .b({8{1'b0}}), .out(adder_5_out), .cin(1'b1));  // open: cout
  Register #(.width(27)) register_6 (.D(adder_4_out), .en(ADD), .clk(Clk), .Q(Mantis_Sum));  // open: clr
  Register #(.width(1)) register_7 (.D(adder_4_cout), .en(ADD), .clk(Clk), .Q(ALU_Carry));  // open: clr
  or or_5 (or_5_out, Mantis_Norm[0], Mantis_Norm[1], Fraction_Norm[0]);
  Multiplexer #(.width(8)) multiplexer_10 (
    .in0(adder_3_out), .in1(adder_5_out), .out(multiplexer_10_out), .sel(A_smaller));
  Register #(.width(1)) register_8 (.D(multiplexer_11_out), .en(CMP), .clk(Clk), .Q(S_L));  // open: clr
  Multiplexer multiplexer_11 (.in0(SA), .in1(SB), .out(multiplexer_11_out), .sel(A_smaller));
  and and_9 (Round_Up, or_5_out, G);
  CU cu_1 (
    .Rst(Rst), .Clk(Clk), .Start(Start), .Check_Done(Check_Done), .INIT(INIT), .LOAD(LOAD), .CMP(CMP),
    .ALIGN(ALIGN), .ADD(ADD), .NORM(NORM), .ROUND(ROUND), .DONE(DONE_t));
  Register register_9 (.D(multiplexer_10_out), .en(CMP), .clk(Clk), .Q(Shift_Amt));  // open: clr
  or or_6 (or_6_out, EA[0], EA[1], EA[2], EA[3], EA[4], EA[5], EA[6], EA[7]);
  or or_7 (or_7_out, EB[0], EB[1], EB[2], EB[3], EB[4], EB[5], EB[6], EB[7]);
  not not_13 (denorm_A, or_6_out);
  not not_14 (denorm_B, or_7_out);
  Register #(.width(1)) register_10 (.D(1'b1), .en(DONE_t), .clk(Clk), .Q(Done), .clr(Start));
  Barrel_Shifter barrel_shifter_1 (
    .Shift_Amt(Shift_Amt), .Mantis_In(Mantis_S), .OUTP(barrel_shifter_1_outp), .Shift_Ovf(Shift_Ovf));
  PE pe_1 (
    .I1(Mantis_Sum[0]), .I2(Mantis_Sum[1]), .I3(Mantis_Sum[2]), .I4(Mantis_Sum[3]), .I5(Mantis_Sum[4]),
    .I6(Mantis_Sum[5]), .I7(Mantis_Sum[6]), .I8(Mantis_Sum[7]), .I9(Mantis_Sum[8]), .I10(Mantis_Sum[9]),
    .I11(Mantis_Sum[10]), .I12(Mantis_Sum[11]), .I13(Mantis_Sum[12]), .I14(Mantis_Sum[13]),
    .I15(Mantis_Sum[14]), .I16(Mantis_Sum[15]), .I17(Mantis_Sum[16]), .I18(Mantis_Sum[17]),
    .I19(Mantis_Sum[18]), .I20(Mantis_Sum[19]), .I21(Mantis_Sum[20]), .I22(Mantis_Sum[21]),
    .I23(Mantis_Sum[22]), .I24(Mantis_Sum[23]), .I25(Mantis_Sum[24]), .I26(Mantis_Sum[25]),
    .I27(Mantis_Sum[26]), .I28(1'b0), .I29(1'b0), .I30(1'b0), .I31(1'b0), .I32(1'b0), .O1(pe_1_o1[0]),
    .O2(pe_1_o1[1]), .O3(pe_1_o1[2]), .O4(pe_1_o1[3]), .O5(pe_1_o1[4]), .Is_Not_Zero(Is_Not_Zero));
  assign not_15_out = ~pe_1_o1;  // NOT_Gate not_15, 5 bits wide
  Adder #(.width(5)) adder_6 (.a(5'b11010), .b(not_15_out), .out(Left_Shift_Amt), .cin(1'b1));  // open: cout
  Comparator #(.mode("unsigned")) comparator_1 (
    .a({3'b000, Left_Shift_Amt}), .b(Exponent_L), .gt(comparator_1_gt), .eq(comparator_1_eq));  // open: lt
  or or_8 (or_8_out, barrel_shifter_1_outp[0], barrel_shifter_1_outp[1], barrel_shifter_1_outp[2], barrel_shifter_1_outp[3], barrel_shifter_1_outp[4], barrel_shifter_1_outp[5], barrel_shifter_1_outp[6], barrel_shifter_1_outp[7], barrel_shifter_1_outp[8], barrel_shifter_1_outp[9], barrel_shifter_1_outp[10], barrel_shifter_1_outp[11], barrel_shifter_1_outp[12], barrel_shifter_1_outp[13], barrel_shifter_1_outp[14], barrel_shifter_1_outp[15], barrel_shifter_1_outp[16], barrel_shifter_1_outp[17], barrel_shifter_1_outp[18], barrel_shifter_1_outp[19], barrel_shifter_1_outp[20], barrel_shifter_1_outp[21]);
  Register #(.width(1)) register_11 (.D(barrel_shifter_1_outp[22]), .en(ALIGN), .clk(Clk), .Q(R_Align));  // open: clr
  Register #(.width(1)) register_12 (.D(barrel_shifter_1_outp[23]), .en(ALIGN), .clk(Clk), .Q(G_Align));  // open: clr
  Register #(.width(24)) register_13 (
    .D(barrel_shifter_1_outp[47:24]), .en(ALIGN), .clk(Clk), .Q(Mantis_S_Aligned));  // open: clr
  or or_9 (or_9_out, comparator_1_gt, comparator_1_eq);
  Multiplexer #(.width(5)) multiplexer_12 (
    .in0(Left_Shift_Amt), .in1({5{1'b0}}), .out(multiplexer_12_out), .sel(or_9_out));
  or or_10 (or_10_out, Shift_Ovf, or_8_out);
  Register #(.width(1)) register_14 (.D(or_10_out), .en(ALIGN), .clk(Clk), .Q(S_Align));  // open: clr
  assign not_16_out = ~{3'b000, multiplexer_12_out};  // NOT_Gate not_16, 8 bits wide
  Multiplexer #(.width(8)) multiplexer_13 (.in0(not_16_out), .in1(8'h1), .out(multiplexer_13_out), .sel(Is_Ovf));
  Bit_Reversal bit_reversal_1 (.INP(Mantis_Sum), .OUTP(bit_reversal_1_outp));
  not not_17 (not_17_out, ALU_Op);
  not not_18 (not_18_out, Is_Ovf);
  and and_10 (Is_Ovf, not_17_out, ALU_Carry);
  Adder adder_7 (.a(Exponent_L), .b(multiplexer_13_out), .out(adder_7_out), .cin(not_18_out), .cout(Exception));
  Shift_27 shift_27_1 (.Shift_Amt(multiplexer_12_out), .Mantis_In(bit_reversal_1_outp), .OUTP(shift_27_1_outp));
  Multiplexer #(.width(8)) multiplexer_14 (
    .in0(adder_7_out), .in1({8{1'b0}}), .out(multiplexer_14_out), .sel(or_9_out));
  Register register_15 (.D(multiplexer_14_out), .en(NORM), .clk(Clk), .Q(EXP_Norm));  // open: clr
  Bit_Reversal bit_reversal_2 (.INP(shift_27_1_outp), .OUTP(bit_reversal_2_outp));
  Shift_27 shift_27_2 (.Shift_Amt(5'b00001), .Mantis_In(Mantis_Sum), .OUTP(shift_27_2_outp));
  Multiplexer #(.width(27)) multiplexer_15 (
    .in0(bit_reversal_2_outp), .in1(shift_27_2_outp), .out(multiplexer_15_out), .sel(Is_Ovf));
  Adder adder_8 (.b({8{1'b0}}), .cin(Check_Done));  // open: a, out, cout
  Register #(.width(27)) register_16 (
    .D(multiplexer_15_out), .en(NORM), .clk(Clk), .Q({Fraction_Norm, G, Mantis_Norm}));  // open: clr

  // Other names for the same wires on the sheet: Mantis_A[22:0] = FA; Mantis_B[22:0] = FB; S = Mantis_Norm[0];
  //   R = Mantis_Norm[1]; Mantis_Norm[26:2] = {Fraction_Norm, G}; LSB = Fraction_Norm[0];
  //   Mantis_Rounded[22:0] = Final_Fraction

  // Notes on the sheet:
  //   ROUND
  //   1.F or 0.F
  //   DONE
  //   ADD
  //   CMP
  //   CU
  //   NORM
  //   ALIGN
endmodule

module CU (
  input  Rst,
  input  Clk,
  input  Start,
  input  Check_Done,
  output INIT,
  output LOAD,
  output CMP,
  output ALIGN,
  output ADD,
  output NORM,
  output ROUND,
  output DONE
);

  wire and_1_out, and_2_out, D_DONE, D_INIT, D_LOAD, D_NORM, not_1_out, not_2_out;

  D_Flip_Flop d_ff_1 (.D(D_INIT), .clk(Clk), .Q(INIT), .preset(Rst));  // open: Qn, reset
  D_Flip_Flop d_ff_2 (.D(D_LOAD), .clk(Clk), .Q(LOAD), .reset(Rst));  // open: Qn, preset
  D_Flip_Flop d_ff_3 (.D(LOAD), .clk(Clk), .Q(CMP), .reset(Rst));  // open: Qn, preset
  D_Flip_Flop d_ff_4 (.D(CMP), .clk(Clk), .Q(ALIGN), .reset(Rst));  // open: Qn, preset
  D_Flip_Flop d_ff_5 (.D(ALIGN), .clk(Clk), .Q(ADD), .reset(Rst));  // open: Qn, preset
  D_Flip_Flop d_ff_6 (.D(D_NORM), .clk(Clk), .Q(NORM), .reset(Rst));  // open: Qn, preset
  D_Flip_Flop d_ff_7 (.D(NORM), .clk(Clk), .Q(ROUND), .reset(Rst));  // open: Qn, preset
  D_Flip_Flop d_ff_8 (.D(D_DONE), .clk(Clk), .Q(DONE), .reset(Rst));  // open: Qn, preset
  not not_1 (not_1_out, Start);
  and and_1 (and_1_out, INIT, not_1_out);
  and and_2 (and_2_out, ROUND, Check_Done);
  not not_2 (not_2_out, Check_Done);
  or or_1 (D_INIT, and_1_out, DONE);
  and and_3 (D_LOAD, INIT, Start);
  or or_2 (D_NORM, ADD, and_2_out);
  and and_4 (D_DONE, ROUND, not_2_out);

  // Other names for the same wires on the sheet: D_ADD = ALIGN; D_ALIGN = CMP; D_CMP = LOAD; D_ROUND = NORM
endmodule

module Barrel_Shifter (
  input  [7:0] Shift_Amt,
  input  [23:0] Mantis_In,
  output [47:0] OUTP,
  output Shift_Ovf
);

  wire or_2_out, or_3_out, or_4_out, or_5_out, or_6_out;
  wire [15:0] multiplexer_4_out;
  wire [31:0] multiplexer_4_out_2;
  wire [47:0] multiplexer_1_out, multiplexer_2_out, multiplexer_3_out;

  or or_1 (Shift_Ovf, Shift_Amt[5], Shift_Amt[6], Shift_Amt[7]);
  Multiplexer #(.width(48)) multiplexer_1 (
    .in0({Mantis_In, {24{1'b0}}}), .in1({1'b0, Mantis_In, {23{1'b0}}}), .out(multiplexer_1_out),
    .sel(or_2_out));
  or or_2 (or_2_out, Shift_Amt[0], Shift_Ovf);
  or or_3 (or_3_out, Shift_Amt[1], Shift_Ovf);
  Multiplexer #(.width(48)) multiplexer_2 (
    .in0(multiplexer_1_out), .in1({2'b00, multiplexer_1_out[47:2]}), .out(multiplexer_2_out), .sel(or_3_out));
  Multiplexer #(.width(48)) multiplexer_3 (
    .in0(multiplexer_2_out), .in1({4'b0000, multiplexer_2_out[47:4]}), .out(multiplexer_3_out), .sel(or_4_out));
  or or_4 (or_4_out, Shift_Amt[2], Shift_Ovf);
  or or_5 (or_5_out, Shift_Amt[3], Shift_Ovf);
  Multiplexer #(.width(48)) multiplexer_4 (
    .in0(multiplexer_3_out), .in1({{8{1'b0}}, multiplexer_3_out[47:8]}),
    .out({multiplexer_4_out_2, multiplexer_4_out}), .sel(or_5_out));
  Multiplexer #(.width(48)) multiplexer_5 (
    .in0({multiplexer_4_out_2, multiplexer_4_out}), .in1({{16{1'b0}}, multiplexer_4_out_2}), .out(OUTP),
    .sel(or_6_out));
  or or_6 (or_6_out, Shift_Amt[4], Shift_Ovf);

  // Other names for the same wires on the sheet: Is_Big = Shift_Ovf; b0 = Shift_Amt[0]; b1 = Shift_Amt[1];
  //   b2 = Shift_Amt[2]; b3 = Shift_Amt[3]; b4 = Shift_Amt[4]
endmodule

module Bit_Reversal (
  input  [26:0] INP,
  output [26:0] OUTP
);


  assign OUTP = {INP[0], INP[1], INP[2], INP[3], INP[4], INP[5], INP[6], INP[7], INP[8], INP[9], INP[10], INP[11], INP[12], INP[13], INP[14], INP[15], INP[16], INP[17], INP[18], INP[19], INP[20], INP[21], INP[22], INP[23], INP[24], INP[25], INP[26]};
endmodule

module Shift_27 (
  input  [4:0] Shift_Amt,
  input  [26:0] Mantis_In,
  output [26:0] OUTP
);

  wire [10:0] multiplexer_4_out_2;
  wire [15:0] multiplexer_4_out;
  wire [26:0] multiplexer_1_out, multiplexer_2_out, multiplexer_3_out;

  Multiplexer #(.width(27)) multiplexer_1 (
    .in0(Mantis_In), .in1({1'b0, Mantis_In[26:1]}), .out(multiplexer_1_out), .sel(Shift_Amt[0]));
  Multiplexer #(.width(27)) multiplexer_2 (
    .in0(multiplexer_1_out), .in1({2'b00, multiplexer_1_out[26:2]}), .out(multiplexer_2_out),
    .sel(Shift_Amt[1]));
  Multiplexer #(.width(27)) multiplexer_3 (
    .in0(multiplexer_2_out), .in1({4'b0000, multiplexer_2_out[26:4]}), .out(multiplexer_3_out),
    .sel(Shift_Amt[2]));
  Multiplexer #(.width(27)) multiplexer_4 (
    .in0(multiplexer_3_out), .in1({{8{1'b0}}, multiplexer_3_out[26:8]}),
    .out({multiplexer_4_out_2, multiplexer_4_out}), .sel(Shift_Amt[3]));
  Multiplexer #(.width(27)) multiplexer_5 (
    .in0({multiplexer_4_out_2, multiplexer_4_out}), .in1({{16{1'b0}}, multiplexer_4_out_2}), .out(OUTP),
    .sel(Shift_Amt[4]));

  // Other names for the same wires on the sheet: b0 = Shift_Amt[0]; b1 = Shift_Amt[1]; b2 = Shift_Amt[2];
  //   b3 = Shift_Amt[3]; b4 = Shift_Amt[4]
endmodule

module Encoder_4_2 (
  input  I0,
  input  I1,
  input  I2,
  input  I3,
  output O0,
  output O1,
  output Valid
);

  wire and_1_out, not_1_out;

  not not_1 (not_1_out, I2);
  and and_1 (and_1_out, not_1_out, I1);
  or or_1 (Valid, I0, I1, I2, I3);
  or or_2 (O0, and_1_out, I3);
  or or_3 (O1, I2, I3);
endmodule

module PE (
  input  I1,
  input  I2,
  input  I3,
  input  I4,
  input  I5,
  input  I6,
  input  I7,
  input  I8,
  input  I9,
  input  I10,
  input  I11,
  input  I12,
  input  I13,
  input  I14,
  input  I15,
  input  I16,
  input  I17,
  input  I18,
  input  I19,
  input  I20,
  input  I21,
  input  I22,
  input  I23,
  input  I24,
  input  I25,
  input  I26,
  input  I27,
  input  I28,
  input  I29,
  input  I30,
  input  I31,
  input  I32,
  output O1,
  output O2,
  output O3,
  output O4,
  output O5,
  output Is_Not_Zero
);

  wire encoder_4_2_1_valid, encoder_4_2_2_valid, encoder_4_2_3_valid, encoder_4_2_4_valid,
       encoder_4_2_5_valid, encoder_4_2_6_valid, encoder_4_2_7_valid, encoder_4_2_8_valid, V_Bot;
  wire [1:0] A0, A1, A2, A3, A4, A5, A6, A7, encoder_4_2_9_o0, encoder_4_2_10_o0;

  Encoder_4_2 encoder_4_2_1 (.I0(I1), .I1(I2), .I2(I3), .I3(I4), .O0(A0[0]), .O1(A0[1]), .Valid(encoder_4_2_1_valid));
  Encoder_4_2 encoder_4_2_2 (.I0(I5), .I1(I6), .I2(I7), .I3(I8), .O0(A1[0]), .O1(A1[1]), .Valid(encoder_4_2_2_valid));
  Encoder_4_2 encoder_4_2_3 (
    .I0(I9), .I1(I10), .I2(I11), .I3(I12), .O0(A2[0]), .O1(A2[1]), .Valid(encoder_4_2_3_valid));
  Encoder_4_2 encoder_4_2_4 (
    .I0(I13), .I1(I14), .I2(I15), .I3(I16), .O0(A3[0]), .O1(A3[1]), .Valid(encoder_4_2_4_valid));
  Encoder_4_2 encoder_4_2_5 (
    .I0(I17), .I1(I18), .I2(I19), .I3(I20), .O0(A4[0]), .O1(A4[1]), .Valid(encoder_4_2_5_valid));
  Encoder_4_2 encoder_4_2_6 (
    .I0(I21), .I1(I22), .I2(I23), .I3(I24), .O0(A5[0]), .O1(A5[1]), .Valid(encoder_4_2_6_valid));
  Encoder_4_2 encoder_4_2_7 (
    .I0(I25), .I1(I26), .I2(I27), .I3(I28), .O0(A6[0]), .O1(A6[1]), .Valid(encoder_4_2_7_valid));
  Encoder_4_2 encoder_4_2_8 (
    .I0(I29), .I1(I30), .I2(I31), .I3(I32), .O0(A7[0]), .O1(A7[1]), .Valid(encoder_4_2_8_valid));
  Encoder_4_2 encoder_4_2_9 (
    .I0(encoder_4_2_1_valid), .I1(encoder_4_2_2_valid), .I2(encoder_4_2_3_valid), .I3(encoder_4_2_4_valid),
    .O0(encoder_4_2_9_o0[0]), .O1(encoder_4_2_9_o0[1]), .Valid(V_Bot));
  Encoder_4_2 encoder_4_2_10 (
    .I0(encoder_4_2_5_valid), .I1(encoder_4_2_6_valid), .I2(encoder_4_2_7_valid), .I3(encoder_4_2_8_valid),
    .O0(encoder_4_2_10_o0[0]), .O1(encoder_4_2_10_o0[1]), .Valid(O5));
  Multiplexer #(.select(3), .width(2)) multiplexer_1 (
    .in0(A0), .in1(A1), .in2(A2), .in3(A3), .in4(A4), .in5(A5), .in6(A6), .in7(A7), .out({O2, O1}),
    .sel({O5, O4, O3}));
  Multiplexer #(.width(2)) multiplexer_2 (.in0(encoder_4_2_9_o0), .in1(encoder_4_2_10_o0), .out({O4, O3}), .sel(O5));
  or or_1 (Is_Not_Zero, O5, V_Bot);

  // Other names for the same wires on the sheet: V_Top = O5
endmodule
